# Fritzing sketch schema (saved by Fritzing 0.9.1b)
breadboards: 1

parts:
  Composant1 = Arduino Nano (Rev3.0)
  Composant2 = SRF05 Ultrasonic Rangefinder

nets:
  GND: Composant1.GND, Composant2.GND
  N1: Composant1.D5, Composant2.Echo
  N2: Composant1.D8, Composant2.Trig
  5V: Composant1.5V, Composant2.VCC
